# Fritzing sketch BME280+LCD-Shield (saved by Fritzing 0.9.3b)

parts:
  Част1 = LCD Keypad Shield
  Част2 = BME280 Breakout

nets:
  N1: Част1.A4(SDA), Част2.SDI/SDA
  N2: Част1.A5(CLK), Част2.SCK/SCL
  +3V3: Част1.+3V3, Част2.3.3V
  GND: Част1.GND, Част2.GND

custom parts:
  LCD Keypad Shield: It consists of a 1602 white character blue backlight LCD. The keypad consists of 5 keys — select, up, right, down and left. To save the digital IO pins, the keypad interface uses only one ADC channel. The key value is read through a 5 stage voltage divider.
