# Fritzing sketch RGB_Controller (saved by Fritzing 1.0.6)
breadboards: 1

parts:
  IR1 = tl1838 [package=THT]
  Част1 = Arduino Uno (Rev3)
  R1 = Resistor [tolerance=±5% power=0.25W resistance=220 package=THT]
  R2 = Resistor [tolerance=±5% power=0.25W resistance=220 package=THT]
  R3 = Resistor [tolerance=±5% power=0.25W resistance=220 package=THT]
  LED1 = RGB LED (com. cathode, rgb) [color="Red (633nm)" current=0.030A package="5 mm [THT]"]

nets:
  N1: IR1.OUT, Част1.D3_PWM
  GND: IR1.GND, Част1.GND, LED1.common_cathode
  VCC: IR1.VCC, Част1.5V
  N2: Част1.D9_PWM, R1.Pin_0
  N3: Част1.D10_PWM/SS, R2.Pin_0
  N4: Част1.D11_PWM/MOSI, R3.Pin_0
  N5: R1.Pin_1, LED1.red_anode
  N6: R2.Pin_1, LED1.green_anode
  N7: R3.Pin_1, LED1.blue_anode

notes:
  TL1838

custom parts:
  tl1838: The TL1838 is a miniaturized receiver for infrared remote control systems. A PIN diode and a preamplifier are assembled on a lead frame, the epoxy package acts as an IR filter. The demodulated output signal can be directly decoded by a microprocessor.
